// Digital circuit Digital.dig as structural Verilog
module Digital (
  input  Manual_Clock,
  input  _50_Hz,
  input  Auto_Clock,
  input  Reset,
  input  Byte_consumed__pulse
);

  wire add_1_c_o, and_1_out, and_2_out, and_3_out, and_4_out, and_5_out, and_7_out, and_8_out, and_9_out,
       and_10_out, and_11_out, Carry_q, decoder_1_out_0, decoder_1_out_1, decoder_1_out_2, decoder_1_out_3,
       decoder_1_out_4, decoder_1_out_5, decoder_1_out_6, decoder_1_out_7, decoder_1_out_8, decoder_1_out_9,
       decoder_1_out_10, decoder_1_out_11, decoder_1_out_12, decoder_1_out_13, decoder_1_out_14,
       decoder_1_out_15, decoder_2_out_0, decoder_2_out_1, decoder_2_out_2, decoder_2_out_3, decoder_2_out_4,
       decoder_2_out_5, decoder_2_out_6, decoder_2_out_7, decoder_2_out_8, decoder_2_out_9, decoder_2_out_14,
       decoder_2_out_15, decoder_3_out_0, decoder_3_out_1, decoder_3_out_2, decoder_3_out_3, decoder_4_out_0,
       decoder_4_out_1, decoder_4_out_2, decoder_4_out_3, decoder_5_out_0, decoder_5_out_1, decoder_5_out_2,
       decoder_5_out_3, decoder_5_out_7, decoder_6_out_0, decoder_6_out_1, decoder_6_out_2, decoder_6_out_3,
       decoder_6_out_4, decoder_6_out_5, decoder_6_out_6, decoder_6_out_7, decoder_7_out_0, decoder_7_out_1,
       decoder_7_out_2, decoder_7_out_3, decoder_7_out_4, decoder_7_out_5, decoder_7_out_6, decoder_7_out_7,
       Neg_q, nor_1_out, not_1_out, or_1_out, or_2_out, or_3_out, or_4_out, or_5_out, or_6_out, or_7_out,
       or_8_out, or_9_out, or_10_out, or_11_out, or_13_out, Output_Buffer_Status_nq, Output_Buffer_Status_q,
       pulldown_3_out, Zero_q;
  wire [3:0] a1_q, a1_q_2, a2_q, a2_q_2, counterpreset_1_out, Microcode_d_2;
  wire [7:0] _8_KB_ROM_d, add_1_s, and_6_out, Character_buffer_2_q, Character_buffer_3_q,
       Character_buffer_4_q, Character_buffer_5_q, Character_buffer_6_q, Character_buffer_7_q,
       Character_buffer_8_q, Character_buffer_q, dh_q, dl_q, driver_6_out, driver_18_out, or_12_out,
       Output_Buffer_q, r1_q, r2_q, r3_q, r4_q, sub_1_s, xor_1_out;
  wire [7:4] counterpreset_1_out_2;
  wire [11:0] IR_q, Microcode_d;
  wire [15:0] _16seg_data_2_d, _16seg_data_3_d, _16seg_data_4_d, _16seg_data_5_d, _16seg_data_6_d,
       _16seg_data_7_d, _16seg_data_8_d, _16seg_data_d, ah_al_q, DC_out_2, PC_out_2, SP_out_2;
  wire [15:8] driver_5_out;
  wire [23:0] Cycle_Counter_out;

  Decoder #(.Selector_Bits(4)) decoder_1 (
    .sel(Microcode_d_2), .out_0(decoder_1_out_0), .out_1(decoder_1_out_1), .out_2(decoder_1_out_2),
    .out_3(decoder_1_out_3), .out_4(decoder_1_out_4), .out_5(decoder_1_out_5), .out_6(decoder_1_out_6),
    .out_7(decoder_1_out_7), .out_8(decoder_1_out_8), .out_9(decoder_1_out_9), .out_10(decoder_1_out_10),
    .out_11(decoder_1_out_11), .out_12(decoder_1_out_12), .out_13(decoder_1_out_13),
    .out_14(decoder_1_out_14), .out_15(decoder_1_out_15));
  or or_1 (or_1_out, decoder_1_out_7, decoder_1_out_8);
  or or_2 (or_2_out, decoder_1_out_9, decoder_1_out_10);
  Decoder #(.Selector_Bits(4)) decoder_2 (
    .sel(Microcode_d[11:8]), .out_0(decoder_2_out_0), .out_1(decoder_2_out_1), .out_2(decoder_2_out_2),
    .out_3(decoder_2_out_3), .out_4(decoder_2_out_4), .out_5(decoder_2_out_5), .out_6(decoder_2_out_6),
    .out_7(decoder_2_out_7), .out_8(decoder_2_out_8), .out_9(decoder_2_out_9), .out_14(decoder_2_out_14),
    .out_15(decoder_2_out_15));  // open: out_10, out_11, out_12, out_13
  or or_3 (or_3_out, decoder_1_out_8, decoder_1_out_10);
  Decoder #(.Selector_Bits(2)) decoder_3 (
    .sel(Microcode_d[7:6]), .out_0(decoder_3_out_0), .out_1(decoder_3_out_1), .out_2(decoder_3_out_2),
    .out_3(decoder_3_out_3));
  and and_1 (and_1_out, _50_Hz, Auto_Clock);
  Decoder #(.Selector_Bits(3)) decoder_4 (
    .sel(Microcode_d[5:3]), .out_0(decoder_4_out_0), .out_1(decoder_4_out_1), .out_2(decoder_4_out_2),
    .out_3(decoder_4_out_3));  // open: out_4, out_5, out_6, out_7
  or or_4 (or_4_out, and_1_out, Manual_Clock);
  or or_5 (or_5_out, Reset, ~or_11_out);  // Or
  Decoder #(.Selector_Bits(3)) decoder_5 (
    .sel(Microcode_d[2:0]), .out_0(decoder_5_out_0), .out_1(decoder_5_out_1), .out_2(decoder_5_out_2),
    .out_3(decoder_5_out_3), .out_7(decoder_5_out_7));  // open: out_4, out_5, out_6
  Counter #(.Bits(24)) Cycle_Counter (.en(1'b1), .C(and_2_out), .clr(1'b0), .out(Cycle_Counter_out));  // open: ovf
  and and_2 (and_2_out, or_4_out, or_5_out);
  LED PC_Out (.in(decoder_3_out_0));
  LED PC_Count (.in(decoder_5_out_0));
  LED PC_In (.in(decoder_4_out_0));
  LED r1_Out (.in(decoder_1_out_0));
  LED r1_In (.in(decoder_2_out_0));
  LED r2_Out (.in(decoder_1_out_1));
  LED r2_In (.in(decoder_2_out_1));
  LED r3_Out (.in(decoder_1_out_2));
  LED r3_In (.in(decoder_2_out_2));
  LED r4_Out (.in(decoder_1_out_3));
  LED r4_In (.in(decoder_2_out_3));
  LED dh_In (.in(decoder_2_out_5));
  LED dh_dl_Out (.in(decoder_3_out_3));
  LED dl_In (.in(decoder_2_out_6));
  LED DC_Out (.in(decoder_3_out_1));
  LED PC_Count_2 (.in(decoder_5_out_1));
  LED DC_In (.in(decoder_4_out_1));
  LED RAM_In (.in(decoder_2_out_4));
  LED Mem_Out (.in(decoder_1_out_4));
  LED SP_Out (.in(decoder_3_out_2));
  LED SP_Inc (.in(decoder_5_out_2));
  LED SP_Dec (.in(decoder_5_out_3));
  LED SP_In (.in(decoder_4_out_2));
  LED ah_Out (.in(decoder_1_out_5));
  LED al_Out (.in(decoder_1_out_6));
  LED al_ah_In (.in(decoder_4_out_3));
  LED IR_In (.in(decoder_2_out_9));
  // Probe on Cycle_Counter_out
  // Probe on {Microcode_d_2, Microcode_d}
  or or_6 (or_6_out, decoder_5_out_7, Reset);
  ROM #(.AddrBits(13), .Bits(16)) Microcode (.A({1'b0, IR_q}), .sel(1'b1), .D({Microcode_d_2, Microcode_d}));
  or or_7 (or_7_out, decoder_5_out_2, decoder_5_out_3);
  not not_1 (not_1_out, and_2_out);
  or or_8 (or_8_out, driver_5_out[13], driver_5_out[14], driver_5_out[15], counterpreset_1_out_2[5]);
  CounterPreset #(.Bits(16)) PC (
    .en(decoder_5_out_0), .C(and_2_out), .dir(1'b0), .in({driver_5_out, driver_6_out}), .ld(decoder_4_out_0),
    .clr(Reset), .out(PC_out_2));  // open: ovf
  Register #(.Bits(8)) r1 (.D(_8_KB_ROM_d), .C(and_2_out), .en(decoder_2_out_0), .Q(r1_q));
  Register #(.Bits(8)) r2 (.D(_8_KB_ROM_d), .C(and_2_out), .en(decoder_2_out_1), .Q(r2_q));
  Register #(.Bits(8)) r3 (.D(_8_KB_ROM_d), .C(and_2_out), .en(decoder_2_out_2), .Q(r3_q));
  Register #(.Bits(8)) r4 (.D(_8_KB_ROM_d), .C(and_2_out), .en(decoder_2_out_3), .Q(r4_q));
  Register #(.Bits(8)) dh (.D(_8_KB_ROM_d), .C(and_2_out), .en(decoder_2_out_5), .Q(dh_q));
  Register #(.Bits(8)) dl (.D(_8_KB_ROM_d), .C(and_2_out), .en(decoder_2_out_6), .Q(dl_q));
  CounterPreset #(.Bits(16)) DC (
    .en(decoder_5_out_1), .C(and_2_out), .dir(1'b0), .in({driver_5_out, driver_6_out}), .ld(decoder_4_out_1),
    .clr(1'b0), .out(DC_out_2));  // open: ovf
  ROM #(.AddrBits(16), .Bits(8)) _8_KB_ROM (.A({driver_5_out, driver_6_out}), .sel(and_3_out), .D(_8_KB_ROM_d));
  RAMSinglePort #(.AddrBits(16), .Bits(8)) _64_KB_RAM (
    .A({driver_5_out, driver_6_out}), .str(decoder_2_out_4), .C(and_2_out), .ld(and_4_out), .D(_8_KB_ROM_d));
  CounterPreset #(.Bits(16)) SP (
    .en(or_7_out), .C(and_2_out), .dir(decoder_5_out_3), .in({driver_5_out, driver_6_out}),
    .ld(decoder_4_out_2), .clr(1'b0), .out(SP_out_2));  // open: ovf
  Register #(.Bits(16)) ah_al (.D({driver_5_out, driver_6_out}), .C(and_2_out), .en(decoder_4_out_3), .Q(ah_al_q));
  Register #(.Bits(8)) IR (.D(_8_KB_ROM_d), .C(and_2_out), .en(decoder_2_out_9), .Q(IR_q[11:4]));
  Counter #(.Bits(3)) Step (.en(1'b1), .C(not_1_out), .clr(or_6_out), .out(IR_q[2:0]));  // open: ovf
  assign _8_KB_ROM_d = decoder_1_out_0 ? r1_q : 8'bz;  // Driver driver_1
  assign _8_KB_ROM_d = decoder_1_out_1 ? r2_q : 8'bz;  // Driver driver_2
  assign _8_KB_ROM_d = decoder_1_out_2 ? r3_q : 8'bz;  // Driver driver_3
  assign _8_KB_ROM_d = decoder_1_out_3 ? r4_q : 8'bz;  // Driver driver_4
  assign driver_5_out = decoder_3_out_3 ? dh_q : 8'bz;  // Driver driver_5
  assign driver_6_out = decoder_3_out_3 ? dl_q : 8'bz;  // Driver driver_6
  assign {driver_5_out, driver_6_out} = decoder_3_out_1 ? DC_out_2 : 16'bz;  // Driver driver_7
  LED ROM_Selected (.in(and_3_out));
  LED RAM_Selected (.in(and_4_out));
  and and_3 (and_3_out, decoder_1_out_4, ~or_8_out);  // And
  and and_4 (and_4_out, decoder_1_out_4, or_8_out);
  assign {driver_5_out, driver_6_out} = decoder_3_out_2 ? SP_out_2 : 16'bz;  // Driver driver_8
  // Probe on IR_q[11:4]
  assign {driver_5_out, driver_6_out} = decoder_3_out_0 ? PC_out_2 : 16'bz;  // Driver driver_9
  assign _8_KB_ROM_d = decoder_1_out_6 ? ah_al_q[7:0] : 8'bz;  // Driver driver_10
  assign _8_KB_ROM_d = decoder_1_out_5 ? ah_al_q[15:8] : 8'bz;  // Driver driver_11
  Decoder #(.Selector_Bits(3)) decoder_6 (
    .sel(IR_q[2:0]), .out_0(decoder_6_out_0), .out_1(decoder_6_out_1), .out_2(decoder_6_out_2),
    .out_3(decoder_6_out_3), .out_4(decoder_6_out_4), .out_5(decoder_6_out_5), .out_6(decoder_6_out_6),
    .out_7(decoder_6_out_7));
  Seven_Seg_Hex seven_seg_hex_1 (.d(driver_5_out[15:12]), .dp(1'b0));
  PullDown #(.Bits(16)) pulldown_1 (.out({driver_5_out, driver_6_out}));
  Seven_Seg_Hex seven_seg_hex_2 (.d(_8_KB_ROM_d[7:4]), .dp(1'b0));
  LED led_1 (.in(decoder_6_out_0));
  LED led_2 (.in(decoder_6_out_1));
  LED led_3 (.in(decoder_6_out_2));
  LED led_4 (.in(decoder_6_out_3));
  LED led_5 (.in(decoder_6_out_4));
  LED led_6 (.in(decoder_6_out_5));
  LED led_7 (.in(decoder_6_out_6));
  LED led_8 (.in(decoder_6_out_7));
  Seven_Seg_Hex seven_seg_hex_3 (.d(driver_5_out[11:8]), .dp(1'b0));
  Seven_Seg_Hex seven_seg_hex_4 (.d(_8_KB_ROM_d[3:0]), .dp(1'b0));
  Multiplexer multiplexer_1 (.sel(IR_q[4]), .in_0(Zero_q), .in_1(Neg_q), .out(IR_q[3]));
  PullDown #(.Bits(8)) pulldown_2 (.out(_8_KB_ROM_d));
  LED CFG_In (.in(decoder_2_out_14));
  CounterPreset #(.Bits(8)) counterpreset_1 (
    .en(1'b0), .C(and_2_out), .dir(1'b0), .in(_8_KB_ROM_d), .ld(decoder_2_out_14), .clr(Reset),
    .out({counterpreset_1_out_2, counterpreset_1_out}));  // open: ovf
  LED CFG_Out (.in(decoder_1_out_14));
  and and_5 (and_5_out, and_2_out, or_9_out);
  LED Update_Flags (.in(or_9_out));
  Seven_Seg_Hex seven_seg_hex_5 (.d(driver_6_out[7:4]), .dp(1'b0));
  or or_9 (or_9_out, or_1_out, or_2_out, decoder_1_out_11, decoder_1_out_12, decoder_1_out_13, decoder_1_out_13);
  assign _8_KB_ROM_d = decoder_1_out_14 ? {counterpreset_1_out_2, counterpreset_1_out} : 8'bz;  // Driver driver_12
  Seven_Seg_Hex seven_seg_hex_6 (.d(driver_6_out[3:0]), .dp(1'b0));
  LED a1_In (.in(decoder_2_out_7));
  LED a2_In (.in(decoder_2_out_8));
  LED Add_Out (.in(or_1_out));
  or or_10 (or_10_out, or_1_out, or_2_out);
  LED Sub_Out (.in(or_2_out));
  LED Or_Out (.in(decoder_1_out_11));
  LED And_Out (.in(decoder_1_out_12));
  LED Xor_Out (.in(decoder_1_out_13));
  LED Use_Carry (.in(or_3_out));
  or or_11 (or_11_out, counterpreset_1_out_2[6], and_9_out);
  LED u_Reset (.in(counterpreset_1_out_2[7]));
  nor nor_1 (nor_1_out, _8_KB_ROM_d[0], _8_KB_ROM_d[1], _8_KB_ROM_d[2], _8_KB_ROM_d[3], _8_KB_ROM_d[4], _8_KB_ROM_d[5], _8_KB_ROM_d[6], _8_KB_ROM_d[7]);
  assign _8_KB_ROM_d = or_1_out ? add_1_s : 8'bz;  // Driver driver_13
  assign _8_KB_ROM_d = or_2_out ? sub_1_s : 8'bz;  // Driver driver_14
  assign _8_KB_ROM_d = decoder_1_out_11 ? or_12_out : 8'bz;  // Driver driver_15
  assign _8_KB_ROM_d = decoder_1_out_12 ? and_6_out : 8'bz;  // Driver driver_16
  assign _8_KB_ROM_d = decoder_1_out_13 ? xor_1_out : 8'bz;  // Driver driver_17
  LED ROM_Disable (.in(counterpreset_1_out_2[5]));
  LED Halt (.in(counterpreset_1_out_2[6]));
  Register #(.Bits(8)) a1 (.D(_8_KB_ROM_d), .C(and_2_out), .en(decoder_2_out_7), .Q({a1_q_2, a1_q}));
  Register #(.Bits(8)) a2 (.D(_8_KB_ROM_d), .C(and_2_out), .en(decoder_2_out_8), .Q({a2_q_2, a2_q}));
  Seven_Seg_Hex seven_seg_hex_7 (.d(counterpreset_1_out), .dp(1'b0));
  D_FF Zero (.D(nor_1_out), .C(and_5_out), .Q(Zero_q));  // open: nQ
  D_FF Neg (.D(_8_KB_ROM_d[7]), .C(and_5_out), .Q(Neg_q));  // open: nQ
  Add #(.Bits(8)) add_1 (.a({a1_q_2, a1_q}), .b({a2_q_2, a2_q}), .c_i(and_8_out), .s(add_1_s), .c_o(add_1_c_o));
  Sub #(.Bits(8)) sub_1 (.a({a1_q_2, a1_q}), .b({a2_q_2, a2_q}), .c_i(and_8_out), .s(sub_1_s));  // open: c_o
  assign or_12_out = {a2_q_2, a2_q} | {a1_q_2, a1_q};  // Or or_12, 8 bits wide
  assign and_6_out = {a2_q_2, a2_q} & {a1_q_2, a1_q};  // And and_6, 8 bits wide
  assign xor_1_out = {a2_q_2, a2_q} ^ {a1_q_2, a1_q};  // XOr xor_1, 8 bits wide
  LED Zero_2 (.in(Zero_q));
  LED Negative (.in(Neg_q));
  // Probe ALU Input 1 on {a1_q_2, a1_q}
  // Probe ALU Input 2 on {a2_q_2, a2_q}
  and and_7 (and_7_out, or_10_out, and_2_out);
  LED Output_Buffer_Empty (.in(Output_Buffer_Status_nq));
  LED Output_In (.in(decoder_2_out_15));
  LED Block_on_output (.in(and_9_out));
  Seven_Seg_Hex seven_seg_hex_8 (.d(a1_q_2), .dp(pulldown_3_out));
  Seven_Seg_Hex seven_seg_hex_9 (.d(a2_q_2), .dp(pulldown_3_out));
  D_FF Carry (.D(add_1_c_o), .C(and_7_out), .Q(Carry_q));  // open: nQ
  and and_8 (and_8_out, or_3_out, Carry_q);
  Seven_Seg_Hex seven_seg_hex_10 (.d(a1_q), .dp(pulldown_3_out));
  Seven_Seg_Hex seven_seg_hex_11 (.d(a2_q), .dp(pulldown_3_out));
  LED Carry_2 (.in(Carry_q));
  and and_9 (and_9_out, ~Output_Buffer_Status_nq, decoder_2_out_15, ~and_2_out);  // And
  PullDown pulldown_3 (.out(pulldown_3_out));
  Decoder #(.Selector_Bits(4)) decoder_7 (
    .sel(counterpreset_1_out), .out_0(decoder_7_out_0), .out_1(decoder_7_out_1), .out_2(decoder_7_out_2),
    .out_3(decoder_7_out_3), .out_4(decoder_7_out_4), .out_5(decoder_7_out_5), .out_6(decoder_7_out_6),
    .out_7(decoder_7_out_7));  // open: out_8, out_9, out_10, out_11, out_12, out_13, out_14, out_15
  LED Input_Out (.in(1'b0));
  LED No_Data (.in(1'b0));
  and and_10 (and_10_out, decoder_2_out_15, ~Output_Buffer_Status_q);  // And
  or or_13 (or_13_out, Output_Buffer_Status_q, and_10_out);
  Register #(.Bits(8)) Character_buffer (
    .D(driver_18_out), .C(and_11_out), .en(decoder_7_out_0), .Q(Character_buffer_q));
  Register #(.Bits(8)) Character_buffer_2 (
    .D(driver_18_out), .C(and_11_out), .en(decoder_7_out_1), .Q(Character_buffer_2_q));
  Register #(.Bits(8)) Character_buffer_3 (
    .D(driver_18_out), .C(and_11_out), .en(decoder_7_out_2), .Q(Character_buffer_3_q));
  Register #(.Bits(8)) Character_buffer_4 (
    .D(driver_18_out), .C(and_11_out), .en(decoder_7_out_3), .Q(Character_buffer_4_q));
  Register #(.Bits(8)) Character_buffer_5 (
    .D(driver_18_out), .C(and_11_out), .en(decoder_7_out_4), .Q(Character_buffer_5_q));
  Register #(.Bits(8)) Character_buffer_6 (
    .D(driver_18_out), .C(and_11_out), .en(decoder_7_out_5), .Q(Character_buffer_6_q));
  Register #(.Bits(8)) Character_buffer_7 (
    .D(driver_18_out), .C(and_11_out), .en(decoder_7_out_6), .Q(Character_buffer_7_q));
  Register #(.Bits(8)) Character_buffer_8 (
    .D(driver_18_out), .C(and_11_out), .en(decoder_7_out_7), .Q(Character_buffer_8_q));
  D_FF_AS Output_Buffer_Status (
    .Set(1'b0), .D(or_13_out), .C(and_2_out), .Clr(and_11_out), .Q(Output_Buffer_Status_q),
    .nQ(Output_Buffer_Status_nq));
  Register #(.Bits(8)) Output_Buffer (.D(_8_KB_ROM_d), .C(and_2_out), .en(and_10_out), .Q(Output_Buffer_q));
  ROM #(.AddrBits(8), .Bits(16)) _16seg_data (.A(Character_buffer_q), .sel(1'b1), .D(_16seg_data_d));
  ROM #(.AddrBits(8), .Bits(16)) _16seg_data_2 (.A(Character_buffer_2_q), .sel(1'b1), .D(_16seg_data_2_d));
  ROM #(.AddrBits(8), .Bits(16)) _16seg_data_3 (.A(Character_buffer_3_q), .sel(1'b1), .D(_16seg_data_3_d));
  ROM #(.AddrBits(8), .Bits(16)) _16seg_data_4 (.A(Character_buffer_4_q), .sel(1'b1), .D(_16seg_data_4_d));
  ROM #(.AddrBits(8), .Bits(16)) _16seg_data_5 (.A(Character_buffer_5_q), .sel(1'b1), .D(_16seg_data_5_d));
  ROM #(.AddrBits(8), .Bits(16)) _16seg_data_6 (.A(Character_buffer_6_q), .sel(1'b1), .D(_16seg_data_6_d));
  ROM #(.AddrBits(8), .Bits(16)) _16seg_data_7 (.A(Character_buffer_7_q), .sel(1'b1), .D(_16seg_data_7_d));
  ROM #(.AddrBits(8), .Bits(16)) _16seg_data_8 (.A(Character_buffer_8_q), .sel(1'b1), .D(_16seg_data_8_d));
  SixteenSeg sixteenseg_1 (.led(_16seg_data_d), .dp(1'b0));
  LED Output_Buffer_Loaded (.in(Output_Buffer_Status_q));
  assign driver_18_out = 1'b1 ? Output_Buffer_q : 8'bz;  // Driver driver_18
  SixteenSeg sixteenseg_2 (.led(_16seg_data_2_d), .dp(1'b0));
  and and_11 (and_11_out, ~and_2_out, Output_Buffer_Status_q);  // And
  SixteenSeg sixteenseg_3 (.led(_16seg_data_3_d), .dp(1'b0));
  SixteenSeg sixteenseg_4 (.led(_16seg_data_4_d), .dp(1'b0));
  SixteenSeg sixteenseg_5 (.led(_16seg_data_5_d), .dp(1'b0));
  SixteenSeg sixteenseg_6 (.led(_16seg_data_6_d), .dp(1'b0));
  SixteenSeg sixteenseg_7 (.led(_16seg_data_7_d), .dp(1'b0));
  SixteenSeg sixteenseg_8 (.led(_16seg_data_8_d), .dp(1'b0));
  LED I_m_sending_a_byte (.in(1'b0));
  LED Send_One_Byte (.in(1'b0));

  // Notes on the sheet:
  //   _50_Hz: Hz: 50
  //   Reset: default 1
  //   Byte_consumed__pulse: default 1
  //   Control Logic Inputs, 12-bits:
  //    - Step (0,1,2,3,4,5,6,7) - 3-bits
  //    - Flags (zero, neg) - 1-bit, selected by lsb of instruction
  //    - Instruction-register - Remaining 8 bits give 256 instructions
  //   Control Logic Outputs:
  //     [12:15] - Data Bus Driver
  //               0 → r1
  //               1 → r2
  //               2 → r3
  //               3 → r4
  //               4 → ram
  //               5 → ah
  //               6 → al
  //               7 → add
  //               8 → add-c
  //               9 → sub
  //               a → sub-c
  //               b → or
  //               c → and
  //               d → xor
  //               e → rshift
  //               f → I/O
  //     [8:11]  - Data Bus Consumer
  //               0 → r1
  //               1 → r2
  //               2 → r3
  //               3 → r4
  //               4 → ram
  //               5 → dh
  //               6 → dl
  //               7 → a1
  //               8 → a2
  //               9 → IR
  //               a → none (Configuration register?)
  //               b → none
  //               c → none
  //               d → none
  //               e → none
  //               f → I/O
  //     [6:7]   - Address Bus Driver
  //               0 → PC
  //               1 → DC
  //               2 → SP
  //               3 → DH/DL
  //     [3:5]   - Address Bus Consumer
  //               0 → PC
  //               1 → DC
  //               2 → SP
  //               3 → AH/AL
  //               4 → none
  //               5 → none
  //               6 → none
  //               7 → none
  //     [0:2]   - Misc
  //               0 → PC Count
  //               1 → DC Count
  //               2 → SP Increase
  //               3 → SP Decrease
  //               4 → none (I/O control?)
  //               5 → none
  //               6 → none
  //               7 → Instruction complete
  //   Data Driver
  //   Data Consumer
  //   Addr
  //   Driver
  //   Address
  //   Consumer
  //   Misc
  //   General Registers
  //   contents of Microcode (hex, n*v repeats v):
  //   4920,27,0,0,0,0,0,0,4920,27,0,0,0,0,0,0,4920,1027,0,0,0,0,0,0,4920,1027,0,0,0,0,0,
  //   0,4920,2027,0,0,0,0,0,0,4920,2027,0,0,0,0,0,0,4920,3027,0,0,0,0,0,0,4920,3027,0,0,
  //   0,0,0,0,4920,127,0,0,0,0,0,0,4920,127,0,0,0,0,0,0,4920,1127,0,0,0,0,0,0,4920,1127,
  //   0,0,0,0,0,0,4920,2127,0,0,0,0,0,0,4920,2127,0,0,0,0,0,0,4920,3127,0,0,0,0,0,0,4920,
  //   3127,0,0,0,0,0,0,4920,227,0,0,0,0,0,0,4920,227,0,0,0,0,0,0,4920,1227,0,0,0,0,0,0,
  //   4920,1227,0,0,0,0,0,0,4920,2227,0,0,0,0,0,0,4920,2227,0,0,0,0,0,0,4920,3227,0,0,0,
  //   0,0,0,4920,3227,0,0,0,0,0,0,4920,327,0,0,0,0,0,0,4920,327,0,0,0,0,0,0,4920,1327,0,
  //   0,0,0,0,0,4920,1327,0,0,0,0,0,0,4920,2327,0,0,0,0,0,0,4920,2327,0,0,0,0,0,0,4920,
  //   3327,0,0,0,0,0,0,4920,3327,0,0,0,0,0,0,4920,4020,a27,0,0,0,0,0,4920,4020,a27,0,0,
  //   0,0,0,4920,4120,a27,0,0,0,0,0,4920,4120,a27,0,0,0,0,0,4920,4220,a27,0,0,0,0,0,4920,
  //   4220,a27,0,0,0,0,0,4920,4320,a27,0,0,0,0,0,4920,4320,a27,0,0,0,0,0,4920,527,0,0,0,
  //   0,0,0,4920,527,0,0,0,0,0,0,4920,1527,0,0,0,0,0,0,4920,1527,0,0,0,0,0,0,4920,2527,
  //   0,0,0,0,0,0,4920,2527,0,0,0,0,0,0,4920,3527,0,0,0,0,0,0,4920,3527,0,0,0,0,0,0,4920,
  //   627,0,0,0,0,0,0,4920,627,0,0,0,0,0,0,4920,1627,0,0,0,0,0,0,4920,1627,0,0,0,0,0,0,
  //   4920,2627,0,0,0,0,0,0,4920,2627,0,0,0,0,0,0,4920,3627,0,0,0,0,0,0,4920,3627,0,0,0,
  //   0,0,0,4920,4520,4620,a27,0,0,0,0,4920,4520,4620,a27,0,0,0,0,4920,acf,0,0,0,0,0,0,
  //   4920,acf,0,0,0,0,0,0,4920,ad7,0,0,0,0,0,0,4920,ad7,0,0,0,0,0,0,4920,a27,0,0,0,0,0,
  //   0,4920,a27,0,0,0,0,0,0,4920,624,40e7,0,0,0,0,0,4920,624,40e7,0,0,0,0,0,4920,1624,
  //   40e7,0,0,0,0,0,4920,1624,40e7,0,0,0,0,0,4920,2624,40e7,0,0,0,0,0,4920,2624,40e7,0,
  //   0,0,0,0,4920,3624,40e7,0,0,0,0,0,4920,3624,40e7,0,0,0,0,0,4920,624,41e7,0,0,0,0,0,
  //   4920,624,41e7,0,0,0,0,0,4920,1624,41e7,0,0,0,0,0,4920,1624,41e7,0,0,0,0,0,4920,2624,
  //   41e7,0,0,0,0,0,4920,2624,41e7,0,0,0,0,0,4920,3624,41e7,0,0,0,0,0,4920,3624,41e7,0,
  //   0,0,0,0,4920,624,42e7,0,0,0,0,0,4920,624,42e7,0,0,0,0,0,4920,1624,42e7,0,0,0,0,0,
  //   4920,1624,42e7,0,0,0,0,0,4920,2624,42e7,0,0,0,0,0,4920,2624,42e7,0,0,0,0,0,4920,3624,
  //   42e7,0,0,0,0,0,4920,3624,42e7,0,0,0,0,0,4920,624,43e7,0,0,0,0,0,4920,624,43e7,0,0,
  //   0,0,0,4920,1624,43e7,0,0,0,0,0,4920,1624,43e7,0,0,0,0,0,4920,2624,43e7,0,0,0,0,0,
  //   4920,2624,43e7,0,0,0,0,0,4920,3624,43e7,0,0,0,0,0,4920,3624,43e7,0,0,0,0,0,4920,624,
  //   4e7,0,0,0,0,0,4920,624,4e7,0,0,0,0,0,4920,624,14e7,0,0,0,0,0,4920,624,14e7,0,0,0,
  //   0,0,4920,624,24e7,0,0,0,0,0,4920,624,24e7,0,0,0,0,0,4920,624,34e7,0,0,0,0,0,4920,
  //   624,34e7,0,0,0,0,0,4920,1624,4e7,0,0,0,0,0,4920,1624,4e7,0,0,0,0,0,4920,1624,14e7,
  //   0,0,0,0,0,4920,1624,14e7,0,0,0,0,0,4920,1624,24e7,0,0,0,0,0,4920,1624,24e7,0,0,0,
  //   0,0,4920,1624,34e7,0,0,0,0,0,4920,1624,34e7,0,0,0,0,0,4920,2624,4e7,0,0,0,0,0,4920,
  //   2624,4e7,0,0,0,0,0,4920,2624,14e7,0,0,0,0,0,4920,2624,14e7,0,0,0,0,0,4920,2624,24e7,
  //   0,0,0,0,0,4920,2624,24e7,0,0,0,0,0,4920,2624,34e7,0,0,0,0,0,4920,2624,34e7,0,0,0,
  //   0,0,4920,3624,4e7,0,0,0,0,0,4920,3624,4e7,0,0,0,0,0,4920,3624,14e7,0,0,0,0,0,4920,
  //   3624,14e7,0,0,0,0,0,4920,3624,24e7,0,0,0,0,0,4920,3624,24e7,0,0,0,0,0,4920,3624,34e7,
  //   0,0,0,0,0,4920,3624,34e7,0,0,0,0,0,4920,4520,4620,40e7,0,0,0,0,4920,4520,4620,40e7,
  //   0,0,0,0,4920,4520,4620,41e7,0,0,0,0,4920,4520,4620,41e7,0,0,0,0,4920,4520,4620,42e7,
  //   0,0,0,0,4920,4520,4620,42e7,0,0,0,0,4920,4520,4620,43e7,0,0,0,0,4920,4520,4620,43e7,
  //   0,0,0,0,4920,4520,4620,4e7,0,0,0,0,4920,4520,4620,4e7,0,0,0,0,4920,4520,4620,14e7,
  //   0,0,0,0,4920,4520,4620,14e7,0,0,0,0,4920,4520,4620,24e7,0,0,0,0,4920,4520,4620,24e7,
  //   0,0,0,0,4920,4520,4620,34e7,0,0,0,0,4920,4520,4620,34e7,0,0,0,0,4920,4061,a27,0,0,
  //   0,0,0,4920,4061,a27,0,0,0,0,0,4920,4161,a27,0,0,0,0,0,4920,4161,a27,0,0,0,0,0,4920,
  //   4261,a27,0,0,0,0,0,4920,4261,a27,0,0,0,0,0,4920,4361,a27,0,0,0,0,0,4920,4361,a27,
  //   0,0,0,0,0,4920,461,a27,0,0,0,0,0,4920,461,a27,0,0,0,0,0,4920,1461,a27,0,0,0,0,0,4920,
  //   1461,a27,0,0,0,0,0,4920,2461,a27,0,0,0,0,0,4920,2461,a27,0,0,0,0,0,4920,3461,a27,
  //   0,0,0,0,0,4920,3461,a27,0,0,0,0,0,4920,40a3,a27,0,0,0,0,0,4920,40a3,a27,0,0,0,0,0,
  //   4920,41a3,a27,0,0,0,0,0,4920,41a3,a27,0,0,0,0,0,4920,42a3,a27,0,0,0,0,0,4920,42a3,
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  //   contents of _8_KB_ROM (hex, n*v repeats v):
  //   66,0,1d,54,55,4,10,0,13,a,9,ab,69,0,18,12,a,a6,12,10,82,66,0,8,81,70,51,50,6e,1c,
  //   20,0,1e,10,1,11,0,9,4,82,6d,0,3,66,0,25
  //   Address Bus
  //   Data Bus
  //   ALU
  //   Output
  //   I/O Select
  //   Configuration Register:
  //       [0:3] → I/O Channel
  //       4
  //       5 → ROM Disable
  //       6 → Halt
  //       7 → Reset
  //   To Do:
  //    - I/O - Single register per direction buffer, single access non-blocking, multi-access blocking.
  //    - Reset line, and to reset at power-on
  //    - More than one "final step" line. Eg: Increment PC + final-step.
  //    - Test add-c / sub-c
  //    - For real-world hardware, aim for non-synchronous reset
  //   Bootstrap Plan:
  //    1. ROM mapped at 0x0000-0x1fff
  //    2. Copy any required code to the end of ram
  //    3. Disable ROM and map RAM to full address space
  //   Input
  //   On the falling edge, Input-Out is set.
  //    -> Assert "send one byte" signal
  //    -> If the I/O device has a byte to send, drive the bus and assert "i'm sending a byte"
  //   On the rising edge:
  //    -> Let the signal in to the bus
  //    -> Store "I'm sending a byte" into a flag
  //   contents of _16seg_data (hex, n*v repeats v):
  //   ff09,3008,eec0,fcc0,31c0,ddc0,dfc0,f100,ffc0,fdc0,f3c0,fc52,cf00,fc12,cfc0,c3c0,8000,
  //   4000,2000,1000,800,400,200,100,80,40,20,10,8,4,2,1,0,410,110,f0d2,ddd2,8809,cee4,
  //   10,4812,8412,ff,d2,1,c0,400,9,ff09,3008,eec0,fcc0,31c0,ddc0,dfc0,f100,ffc0,fdc0,8400,
  //   8001,c,cc0,21,e142,fe82,f3c0,fc52,cf00,fc12,cfc0,c3c0,df40,33c0,cc12,3e00,38c,f00,
  //   3328,3324,ff00,e3c0,ff04,e3c4,ddc0,c012,3f00,309,3f02,2d,21c2,cc09,8700,24,7800,120,
  //   c00,20,f3c0,fc52,cf00,fc12,cfc0,c3c0,df40,33c0,cc12,3e00,38c,f00,3328,3324,ff00,e3c0,
  //   ff04,e3c4,ddc0,c012,3f00,309,3f02,2d,21c2,cc09,4892,12,8452,a150
  //   contents of _16seg_data_2 (hex, n*v repeats v):
  //   ff09,3008,eec0,fcc0,31c0,ddc0,dfc0,f100,ffc0,fdc0,f3c0,fc52,cf00,fc12,cfc0,c3c0,8000,
  //   4000,2000,1000,800,400,200,100,80,40,20,10,8,4,2,1,0,410,110,f0d2,ddd2,8809,cee4,
  //   10,4812,8412,ff,d2,1,c0,400,9,ff09,3008,eec0,fcc0,31c0,ddc0,dfc0,f100,ffc0,fdc0,8400,
  //   8001,c,cc0,21,e142,fe82,f3c0,fc52,cf00,fc12,cfc0,c3c0,df40,33c0,cc12,3e00,38c,f00,
  //   3328,3324,ff00,e3c0,ff04,e3c4,ddc0,c012,3f00,309,3f02,2d,21c2,cc09,8700,24,7800,120,
  //   c00,20,f3c0,fc52,cf00,fc12,cfc0,c3c0,df40,33c0,cc12,3e00,38c,f00,3328,3324,ff00,e3c0,
  //   ff04,e3c4,ddc0,c012,3f00,309,3f02,2d,21c2,cc09,4892,12,8452,a150
  //   contents of _16seg_data_3 (hex, n*v repeats v):
  //   ff09,3008,eec0,fcc0,31c0,ddc0,dfc0,f100,ffc0,fdc0,f3c0,fc52,cf00,fc12,cfc0,c3c0,8000,
  //   4000,2000,1000,800,400,200,100,80,40,20,10,8,4,2,1,0,410,110,f0d2,ddd2,8809,cee4,
  //   10,4812,8412,ff,d2,1,c0,400,9,ff09,3008,eec0,fcc0,31c0,ddc0,dfc0,f100,ffc0,fdc0,8400,
  //   8001,c,cc0,21,e142,fe82,f3c0,fc52,cf00,fc12,cfc0,c3c0,df40,33c0,cc12,3e00,38c,f00,
  //   3328,3324,ff00,e3c0,ff04,e3c4,ddc0,c012,3f00,309,3f02,2d,21c2,cc09,8700,24,7800,120,
  //   c00,20,f3c0,fc52,cf00,fc12,cfc0,c3c0,df40,33c0,cc12,3e00,38c,f00,3328,3324,ff00,e3c0,
  //   ff04,e3c4,ddc0,c012,3f00,309,3f02,2d,21c2,cc09,4892,12,8452,a150
  //   contents of _16seg_data_4 (hex, n*v repeats v):
  //   ff09,3008,eec0,fcc0,31c0,ddc0,dfc0,f100,ffc0,fdc0,f3c0,fc52,cf00,fc12,cfc0,c3c0,8000,
  //   4000,2000,1000,800,400,200,100,80,40,20,10,8,4,2,1,0,410,110,f0d2,ddd2,8809,cee4,
  //   10,4812,8412,ff,d2,1,c0,400,9,ff09,3008,eec0,fcc0,31c0,ddc0,dfc0,f100,ffc0,fdc0,8400,
  //   8001,c,cc0,21,e142,fe82,f3c0,fc52,cf00,fc12,cfc0,c3c0,df40,33c0,cc12,3e00,38c,f00,
  //   3328,3324,ff00,e3c0,ff04,e3c4,ddc0,c012,3f00,309,3f02,2d,21c2,cc09,8700,24,7800,120,
  //   c00,20,f3c0,fc52,cf00,fc12,cfc0,c3c0,df40,33c0,cc12,3e00,38c,f00,3328,3324,ff00,e3c0,
  //   ff04,e3c4,ddc0,c012,3f00,309,3f02,2d,21c2,cc09,4892,12,8452,a150
  //   contents of _16seg_data_5 (hex, n*v repeats v):
  //   ff09,3008,eec0,fcc0,31c0,ddc0,dfc0,f100,ffc0,fdc0,f3c0,fc52,cf00,fc12,cfc0,c3c0,8000,
  //   4000,2000,1000,800,400,200,100,80,40,20,10,8,4,2,1,0,410,110,f0d2,ddd2,8809,cee4,
  //   10,4812,8412,ff,d2,1,c0,400,9,ff09,3008,eec0,fcc0,31c0,ddc0,dfc0,f100,ffc0,fdc0,8400,
  //   8001,c,cc0,21,e142,fe82,f3c0,fc52,cf00,fc12,cfc0,c3c0,df40,33c0,cc12,3e00,38c,f00,
  //   3328,3324,ff00,e3c0,ff04,e3c4,ddc0,c012,3f00,309,3f02,2d,21c2,cc09,8700,24,7800,120,
  //   c00,20,f3c0,fc52,cf00,fc12,cfc0,c3c0,df40,33c0,cc12,3e00,38c,f00,3328,3324,ff00,e3c0,
  //   ff04,e3c4,ddc0,c012,3f00,309,3f02,2d,21c2,cc09,4892,12,8452,a150
  //   contents of _16seg_data_6 (hex, n*v repeats v):
  //   ff09,3008,eec0,fcc0,31c0,ddc0,dfc0,f100,ffc0,fdc0,f3c0,fc52,cf00,fc12,cfc0,c3c0,8000,
  //   4000,2000,1000,800,400,200,100,80,40,20,10,8,4,2,1,0,410,110,f0d2,ddd2,8809,cee4,
  //   10,4812,8412,ff,d2,1,c0,400,9,ff09,3008,eec0,fcc0,31c0,ddc0,dfc0,f100,ffc0,fdc0,8400,
  //   8001,c,cc0,21,e142,fe82,f3c0,fc52,cf00,fc12,cfc0,c3c0,df40,33c0,cc12,3e00,38c,f00,
  //   3328,3324,ff00,e3c0,ff04,e3c4,ddc0,c012,3f00,309,3f02,2d,21c2,cc09,8700,24,7800,120,
  //   c00,20,f3c0,fc52,cf00,fc12,cfc0,c3c0,df40,33c0,cc12,3e00,38c,f00,3328,3324,ff00,e3c0,
  //   ff04,e3c4,ddc0,c012,3f00,309,3f02,2d,21c2,cc09,4892,12,8452,a150
  //   contents of _16seg_data_7 (hex, n*v repeats v):
  //   ff09,3008,eec0,fcc0,31c0,ddc0,dfc0,f100,ffc0,fdc0,f3c0,fc52,cf00,fc12,cfc0,c3c0,8000,
  //   4000,2000,1000,800,400,200,100,80,40,20,10,8,4,2,1,0,410,110,f0d2,ddd2,8809,cee4,
  //   10,4812,8412,ff,d2,1,c0,400,9,ff09,3008,eec0,fcc0,31c0,ddc0,dfc0,f100,ffc0,fdc0,8400,
  //   8001,c,cc0,21,e142,fe82,f3c0,fc52,cf00,fc12,cfc0,c3c0,df40,33c0,cc12,3e00,38c,f00,
  //   3328,3324,ff00,e3c0,ff04,e3c4,ddc0,c012,3f00,309,3f02,2d,21c2,cc09,8700,24,7800,120,
  //   c00,20,f3c0,fc52,cf00,fc12,cfc0,c3c0,df40,33c0,cc12,3e00,38c,f00,3328,3324,ff00,e3c0,
  //   ff04,e3c4,ddc0,c012,3f00,309,3f02,2d,21c2,cc09,4892,12,8452,a150
  //   contents of _16seg_data_8 (hex, n*v repeats v):
  //   ff09,3008,eec0,fcc0,31c0,ddc0,dfc0,f100,ffc0,fdc0,f3c0,fc52,cf00,fc12,cfc0,c3c0,8000,
  //   4000,2000,1000,800,400,200,100,80,40,20,10,8,4,2,1,0,410,110,f0d2,ddd2,8809,cee4,
  //   10,4812,8412,ff,d2,1,c0,400,9,ff09,3008,eec0,fcc0,31c0,ddc0,dfc0,f100,ffc0,fdc0,8400,
  //   8001,c,cc0,21,e142,fe82,f3c0,fc52,cf00,fc12,cfc0,c3c0,df40,33c0,cc12,3e00,38c,f00,
  //   3328,3324,ff00,e3c0,ff04,e3c4,ddc0,c012,3f00,309,3f02,2d,21c2,cc09,8700,24,7800,120,
  //   c00,20,f3c0,fc52,cf00,fc12,cfc0,c3c0,df40,33c0,cc12,3e00,38c,f00,3328,3324,ff00,e3c0,
  //   ff04,e3c4,ddc0,c012,3f00,309,3f02,2d,21c2,cc09,4892,12,8452,a150
endmodule
