// Digital circuit adder-subtractor-component.dig as structural Verilog
module adder_subtractor_component (
  input  [7:0] A,
  input  [7:0] B,
  input  C_i,
  input  Sub,
  output [7:0] R,
  output C_o
);

  wire and_1_out, and_2_out, and_3_out, and_4_out, and_5_out, and_6_out, and_7_out, and_8_out, and_9_out,
       and_10_out, and_11_out, and_12_out, and_13_out, and_14_out, and_15_out, and_16_out, or_2_out,
       or_3_out, or_4_out, or_5_out, or_6_out, or_7_out, or_8_out, xor_1_out, xor_2_out, xor_3_out,
       xor_5_out, xor_6_out, xor_7_out, xor_9_out, xor_10_out, xor_11_out, xor_13_out, xor_14_out,
       xor_15_out, xor_17_out, xor_18_out, xor_19_out, xor_21_out, xor_22_out, xor_23_out, xor_25_out,
       xor_26_out, xor_27_out, xor_29_out, xor_30_out, xor_31_out;

  or or_1 (C_o, and_2_out, and_1_out);
  and and_1 (and_1_out, B[7], xor_1_out);
  and and_2 (and_2_out, xor_2_out, or_2_out);
  xor xor_1 (xor_1_out, A[7], Sub);
  xor xor_2 (xor_2_out, xor_3_out, Sub);
  xor xor_3 (xor_3_out, B[7], A[7]);
  xor xor_4 (R[7], or_2_out, xor_3_out);
  or or_2 (or_2_out, and_4_out, and_3_out);
  xor xor_5 (xor_5_out, A[6], Sub);
  and and_3 (and_3_out, B[6], xor_5_out);
  and and_4 (and_4_out, xor_6_out, or_3_out);
  xor xor_6 (xor_6_out, xor_7_out, Sub);
  xor xor_7 (xor_7_out, B[6], A[6]);
  xor xor_8 (R[6], or_3_out, xor_7_out);
  or or_3 (or_3_out, and_6_out, and_5_out);
  and and_5 (and_5_out, B[5], xor_9_out);
  and and_6 (and_6_out, xor_10_out, or_4_out);
  xor xor_9 (xor_9_out, A[5], Sub);
  xor xor_10 (xor_10_out, xor_11_out, Sub);
  xor xor_11 (xor_11_out, B[5], A[5]);
  xor xor_12 (R[5], or_4_out, xor_11_out);
  or or_4 (or_4_out, and_8_out, and_7_out);
  xor xor_13 (xor_13_out, A[4], Sub);
  and and_7 (and_7_out, B[4], xor_13_out);
  and and_8 (and_8_out, xor_14_out, or_5_out);
  xor xor_14 (xor_14_out, xor_15_out, Sub);
  xor xor_15 (xor_15_out, B[4], A[4]);
  xor xor_16 (R[4], or_5_out, xor_15_out);
  or or_5 (or_5_out, and_10_out, and_9_out);
  and and_9 (and_9_out, B[3], xor_17_out);
  and and_10 (and_10_out, xor_18_out, or_6_out);
  xor xor_17 (xor_17_out, A[3], Sub);
  xor xor_18 (xor_18_out, xor_19_out, Sub);
  xor xor_19 (xor_19_out, B[3], A[3]);
  xor xor_20 (R[3], or_6_out, xor_19_out);
  or or_6 (or_6_out, and_12_out, and_11_out);
  xor xor_21 (xor_21_out, A[2], Sub);
  and and_11 (and_11_out, B[2], xor_21_out);
  and and_12 (and_12_out, xor_22_out, or_7_out);
  xor xor_22 (xor_22_out, xor_23_out, Sub);
  xor xor_23 (xor_23_out, B[2], A[2]);
  xor xor_24 (R[2], or_7_out, xor_23_out);
  or or_7 (or_7_out, and_14_out, and_13_out);
  and and_13 (and_13_out, B[1], xor_25_out);
  and and_14 (and_14_out, xor_26_out, or_8_out);
  xor xor_25 (xor_25_out, A[1], Sub);
  xor xor_26 (xor_26_out, xor_27_out, Sub);
  xor xor_27 (xor_27_out, B[1], A[1]);
  xor xor_28 (R[1], or_8_out, xor_27_out);
  or or_8 (or_8_out, and_16_out, and_15_out);
  xor xor_29 (xor_29_out, A[0], Sub);
  and and_15 (and_15_out, B[0], xor_29_out);
  and and_16 (and_16_out, xor_30_out, C_i);
  xor xor_30 (xor_30_out, xor_31_out, Sub);
  xor xor_31 (xor_31_out, B[0], A[0]);
  xor xor_32 (R[0], C_i, xor_31_out);

  // Notes on the sheet:
  //   Sub: Subtracts when high
  //   R: Result
  //   Set during register load to allow  for propagation delay
endmodule
