// Digital circuit adder-subtractor.dig as structural Verilog
module adder_subtractor (
  input  in_1,
  input  in_2,
  input  in_3,
  input  in_4,
  input  in_5,
  input  in_6,
  input  in_7,
  input  in_8,
  input  in_9,
  input  in_10,
  input  in_11,
  input  in_12,
  input  in_13,
  input  in_14,
  input  in_15,
  input  in_16,
  input  in_17,
  input  in_18,
  input  in_19,
  input  in_20,
  input  in_21,
  input  in_22,
  input  in_23,
  input  in_24,
  input  in_25,
  input  in_26,
  input  in_27,
  input  A_0,
  input  B_0,
  input  Carry___Borrow,
  input  Add___Sub,
  input  A_1,
  input  B_1,
  input  A_2,
  input  B_2,
  input  A_3,
  input  B_3,
  input  A_4,
  input  B_4,
  input  A_5,
  input  B_5,
  input  A_6,
  input  B_6,
  input  A_7,
  input  B_7
);

  wire add_1_c_o, and_1_out, and_2_out, and_4_out, and_5_out, and_6_out, and_7_out, and_8_out, and_9_out,
       and_10_out, and_11_out, and_12_out, and_13_out, and_14_out, and_15_out, and_16_out, and_17_out,
       and_18_out, and_19_out, and_20_out, and_21_out, and_22_out, and_23_out, and_24_out, not_1_out,
       or_1_out, or_2_out, or_3_out, or_4_out, or_5_out, or_6_out, or_7_out, or_8_out, sub_1_c_o, xor_1_out,
       xor_2_out, xor_3_out, xor_4_out, xor_5_out, xor_6_out, xor_7_out, xor_8_out, xor_9_out, xor_10_out,
       xor_11_out, xor_12_out, xor_13_out, xor_14_out, xor_16_out, xor_17_out, xor_18_out, xor_19_out,
       xor_20_out, xor_21_out, xor_22_out, xor_23_out, xor_25_out, xor_26_out, xor_27_out, xor_29_out,
       xor_30_out, xor_31_out, xor_33_out, xor_34_out, xor_35_out, xor_37_out, xor_38_out, xor_39_out,
       xor_41_out, xor_42_out, xor_43_out, xor_45_out, xor_46_out, xor_47_out;
  wire [7:0] add_1_s, neg_1_out, neg_2_out, sub_1_s, xor_15_out;

  LED led_1 (.in(neg_1_out[6]));
  LED led_2 (.in(neg_1_out[7]));
  LED led_3 (.in(xor_7_out));
  LED led_4 (.in(xor_8_out));
  LED led_5 (.in(neg_1_out[4]));
  LED led_6 (.in(neg_1_out[5]));
  LED led_7 (.in(xor_5_out));
  LED led_8 (.in(xor_6_out));
  LED led_9 (.in(neg_1_out[3]));
  LED led_10 (.in(xor_4_out));
  LED led_11 (.in(or_1_out));
  Neg #(.Bits(8)) neg_1 (.in({in_2, in_3, in_4, in_5, in_6, in_7, in_8, in_9}), .out(neg_1_out));
  LED led_12 (.in(neg_1_out[1]));
  LED led_13 (.in(neg_1_out[2]));
  LED led_14 (.in(xor_2_out));
  LED led_15 (.in(xor_3_out));
  or or_1 (or_1_out, and_2_out, and_1_out);
  LED led_16 (.in(neg_1_out[0]));
  LED led_17 (.in(xor_1_out));
  xor xor_1 (xor_1_out, xor_20_out, in_1);
  xor xor_2 (xor_2_out, and_11_out, xor_19_out);
  xor xor_3 (xor_3_out, and_12_out, xor_18_out);
  xor xor_4 (xor_4_out, and_7_out, xor_16_out);
  xor xor_5 (xor_5_out, and_8_out, xor_17_out);
  xor xor_6 (xor_6_out, and_6_out, xor_13_out);
  xor xor_7 (xor_7_out, and_4_out, xor_12_out);
  xor xor_8 (xor_8_out, and_5_out, xor_10_out);
  xor xor_9 (xor_9_out, A_7, Add___Sub);
  and and_1 (and_1_out, B_7, xor_9_out);
  and and_2 (and_2_out, xor_11_out, or_2_out);
  xor xor_10 (xor_10_out, in_2, in_1);
  // And and_3 has open pins: In_1=and_5_out, In_2=xor_10_out, out=open
  xor xor_11 (xor_11_out, xor_14_out, Add___Sub);
  xor xor_12 (xor_12_out, in_3, in_1);
  xor xor_13 (xor_13_out, in_4, in_1);
  and and_4 (and_4_out, and_6_out, xor_13_out);
  and and_5 (and_5_out, and_4_out, xor_12_out);
  xor xor_14 (xor_14_out, B_7, A_7);
  xor xor_15 (xor_15_out[7], or_2_out, xor_14_out);
  LED led_18 (.in(xor_15_out[7]));
  xor xor_16 (xor_16_out, in_6, in_1);
  xor xor_17 (xor_17_out, in_5, in_1);
  and and_6 (and_6_out, and_8_out, xor_17_out);
  or or_2 (or_2_out, and_10_out, and_9_out);
  xor xor_18 (xor_18_out, in_7, in_1);
  xor xor_19 (xor_19_out, in_8, in_1);
  and and_7 (and_7_out, and_12_out, xor_18_out);
  and and_8 (and_8_out, and_7_out, xor_16_out);
  and and_9 (and_9_out, B_6, xor_21_out);
  and and_10 (and_10_out, xor_22_out, or_3_out);
  xor xor_20 (xor_20_out, in_9, in_1);
  and and_11 (and_11_out, in_1, xor_20_out);
  and and_12 (and_12_out, and_11_out, xor_19_out);
  xor xor_21 (xor_21_out, A_6, Add___Sub);
  xor xor_22 (xor_22_out, xor_23_out, Add___Sub);
  xor xor_23 (xor_23_out, B_6, A_6);
  xor xor_24 (xor_15_out[6], or_3_out, xor_23_out);
  LED led_19 (.in(xor_15_out[6]));
  or or_3 (or_3_out, and_14_out, and_13_out);
  xor xor_25 (xor_25_out, A_5, Add___Sub);
  and and_13 (and_13_out, B_5, xor_25_out);
  and and_14 (and_14_out, xor_26_out, or_4_out);
  xor xor_26 (xor_26_out, xor_27_out, Add___Sub);
  xor xor_27 (xor_27_out, B_5, A_5);
  xor xor_28 (xor_15_out[5], or_4_out, xor_27_out);
  LED led_20 (.in(xor_15_out[5]));
  // Probe on {in_10, in_11, in_12, in_13, in_14, in_15, in_16, in_17}
  // Probe on {in_18, in_19, in_20, in_21, in_22, in_23, in_24, in_25}
  or or_4 (or_4_out, and_16_out, and_15_out);
  Neg #(.Bits(8)) neg_2 (.in({in_18, in_19, in_20, in_21, in_22, in_23, in_24, in_25}), .out(neg_2_out));
  and and_15 (and_15_out, B_4, xor_29_out);
  and and_16 (and_16_out, xor_30_out, or_5_out);
  Sub #(.Bits(8)) sub_1 (
    .a({in_10, in_11, in_12, in_13, in_14, in_15, in_16, in_17}),
    .b({in_18, in_19, in_20, in_21, in_22, in_23, in_24, in_25}), .c_i(in_27), .s(sub_1_s), .c_o(sub_1_c_o));
  Add #(.Bits(8)) add_1 (
    .a({in_10, in_11, in_12, in_13, in_14, in_15, in_16, in_17}), .b(neg_2_out), .c_i(in_26), .s(add_1_s),
    .c_o(add_1_c_o));
  xor xor_29 (xor_29_out, A_4, Add___Sub);
  xor xor_30 (xor_30_out, xor_31_out, Add___Sub);
  // Probe on sub_1_s
  // Probe on add_1_s
  not not_1 (not_1_out, add_1_c_o);
  xor xor_31 (xor_31_out, B_4, A_4);
  xor xor_32 (xor_15_out[4], or_5_out, xor_31_out);
  LED led_21 (.in(xor_15_out[4]));
  LED led_22 (.in(sub_1_c_o));
  LED led_23 (.in(not_1_out));
  or or_5 (or_5_out, and_18_out, and_17_out);
  xor xor_33 (xor_33_out, A_3, Add___Sub);
  and and_17 (and_17_out, B_3, xor_33_out);
  and and_18 (and_18_out, xor_34_out, or_6_out);
  xor xor_34 (xor_34_out, xor_35_out, Add___Sub);
  xor xor_35 (xor_35_out, B_3, A_3);
  xor xor_36 (xor_15_out[3], or_6_out, xor_35_out);
  LED led_24 (.in(xor_15_out[3]));
  or or_6 (or_6_out, and_20_out, and_19_out);
  and and_19 (and_19_out, B_2, xor_37_out);
  and and_20 (and_20_out, xor_38_out, or_7_out);
  xor xor_37 (xor_37_out, A_2, Add___Sub);
  xor xor_38 (xor_38_out, xor_39_out, Add___Sub);
  xor xor_39 (xor_39_out, B_2, A_2);
  xor xor_40 (xor_15_out[2], or_7_out, xor_39_out);
  LED led_25 (.in(xor_15_out[2]));
  or or_7 (or_7_out, and_22_out, and_21_out);
  xor xor_41 (xor_41_out, A_1, Add___Sub);
  and and_21 (and_21_out, B_1, xor_41_out);
  and and_22 (and_22_out, xor_42_out, or_8_out);
  xor xor_42 (xor_42_out, xor_43_out, Add___Sub);
  xor xor_43 (xor_43_out, B_1, A_1);
  xor xor_44 (xor_15_out[1], or_8_out, xor_43_out);
  LED led_26 (.in(xor_15_out[1]));
  or or_8 (or_8_out, and_24_out, and_23_out);
  and and_23 (and_23_out, B_0, xor_45_out);
  and and_24 (and_24_out, xor_46_out, Carry___Borrow);
  xor xor_45 (xor_45_out, A_0, Add___Sub);
  xor xor_46 (xor_46_out, xor_47_out, Add___Sub);
  xor xor_47 (xor_47_out, B_0, A_0);
  xor xor_48 (xor_15_out[0], Carry___Borrow, xor_47_out);
  LED led_27 (.in(xor_15_out[0]));
  // Probe on {A_7, A_6, A_5, A_4, A_3, A_2, A_1, A_0}
  // Probe on {B_7, B_6, B_5, B_4, B_3, B_2, B_1, B_0}
  // Probe on xor_15_out

  // Notes on the sheet:
  //   Set during register load to allow  for propagation delay
endmodule
